# Fritzing sketch Arduino-nano-sense-with-Neopixel-and-external-power (saved by Fritzing 1.0.1rc)

parts:
  Dfrobot_-_NeoPixel_24 = 24 NeoPixel Ring [part_number=1586]
  Nano-33-ble-sense = Arduino Nano 33 BLE Sense
  V1 = DC Power [voltage=5]

nets:
  N1: Dfrobot_-_NeoPixel_24.IN, Nano-33-ble-sense.D3~
  GND: Dfrobot_-_NeoPixel_24.GND, Nano-33-ble-sense.GND, V1.V-
  VDD: Dfrobot_-_NeoPixel_24.VDD, Nano-33-ble-sense.3V3
  N2: Nano-33-ble-sense.VIN, V1.V+

custom parts:
  24 NeoPixel Ring: 24 ultra bright smart LED NeoPixels are arranged in a circle with 2.6" (66mm) outer diameter. The rings are 'chainable' - connect the output pin of one to the input pin of another. Use only one microcontroller pin to control as many as you can chain together! Each LED is addressable as the driver chip is inside the LED. Each one has ~18mA constant current drive so the color will be very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
  Arduino Nano 33 BLE Sense: The Nano 33 BLE Sense (without headers) is Arduino’s 3.3V AI enabled board in the smallest available form factor: 45x18mm! The Arduino Nano 33 BLE Sense is a completely new board on a well-known form factor. It comes with a series of embedded sensors: 9 axis inertial sensor: what makes this board ideal for wearable devices humidity, and temperature sensor: to get highly accurate measurements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
