# Fritzing sketch Arduino-nano-sense-with-Neopixel-and-external-power_V1 (saved by Fritzing 1.0.1rc)
stripboards: 1

parts:
  NeoPixel_Ring_24 = 24 NeoPixel Ring [part_number=1586]
  U1 = LIPO-2000mAh [package=lipo-2000]
  Lipo = Adafruit MicroLipo Charger USB Type C [part_number="Adafruit #4410"]
  Nano-33-ble-sense = Arduino Nano 33 BLE Sense

nets:
  N1: NeoPixel_Ring_24.IN, Nano-33-ble-sense.D3~
  VDD: NeoPixel_Ring_24.VDD, Nano-33-ble-sense.D11/MOSI, Nano-33-ble-sense.+5V
  GND: NeoPixel_Ring_24.GND, U1.-, Lipo.GND, Nano-33-ble-sense.GND
  N2: U1.+, Lipo.VBAT
  5V: Lipo.5V, Nano-33-ble-sense.VIN

custom parts:
  24 NeoPixel Ring: 24 ultra bright smart LED NeoPixels are arranged in a circle with 2.6" (66mm) outer diameter. The rings are 'chainable' - connect the output pin of one to the input pin of another. Use only one microcontroller pin to control as many as you can chain together! Each LED is addressable as the driver chip is inside the LED. Each one has ~18mA constant current drive so the color will be very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
  Adafruit MicroLipo Charger USB Type C: Oh so handy, this little lipo charger is so small and easy to use you can keep it on your desk or mount it easily into any project! Simply plug it via any USB C cable into a USB port and a 3.7V/4.2V lithium polymer or lithium ion rechargeable battery into the JST plug on the other end. There are two LEDs - one red and one green. While charging, the red LED is lit. When the battery is fully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
  Arduino Nano 33 BLE Sense: The Nano 33 BLE Sense (without headers) is Arduino’s 3.3V AI enabled board in the smallest available form factor: 45x18mm! The Arduino Nano 33 BLE Sense is a completely new board on a well-known form factor. It comes with a series of embedded sensors: 9 axis inertial sensor: what makes this board ideal for wearable devices humidity, and temperature sensor: to get highly accurate measurements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
